# Fritzing sketch wiring (saved by Fritzing 0.9.0b)
breadboards: 1

parts:
  IC3 = A7105 [chip_label=IC package="DIP (Dual Inline) [THT]"]
  Bauteil1 = Arduino Pro Mini v13  # not connected
  S1 = Pushbutton [package="[THT]"]
  LED1 = LED - 5mm [color="Green (555nm)" package="5 mm [THT]"]
  LED2 = LED - 5mm [color="Red (633nm)" package="5 mm [THT]"]
  R2 = Resistor [tolerance=±5% resistance=220 package=THT]
  Bauteil3 = Arduino Pro Micro

nets:
  N1: IC3.pin1, IC3.pin10, S1.Pin_1, S1.Pin_2, R2.Pin_1
  N2: IC3.pin6, LED1.cathode, Bauteil3.D0/TX, Bauteil3.GND
  N3: IC3.pin9, Bauteil3.A1, Bauteil3.A0, Bauteil3.D9_PWM, Bauteil3.D8
  N4: IC3.pin12, Bauteil3.D1/RX
  N5: IC3.pin13, Bauteil3.A4, Bauteil3.A5
  N6: IC3.pin14, Bauteil3.VCC
  N7: S1.Pin_3, S1.Pin_4, Bauteil3.D10_PWM/SS
  N8: LED1.anode, LED2.anode, R2.Pin_0
  N9: LED2.cathode, Bauteil3.DTR

custom parts:
  A7105: A DIP stand-in part for whatever IC you want. With 14 pins on a 300mil dual inline package (DIP) footprint.
  Arduino Pro Micro: It's blue! It's thin! It's the Arduino Pro Mini! SparkFun's minimal design approach to Arduino. This is a 5V Arduino running the 16MHz bootloader. Arduino Pro Mini does not come with connectors populated so that you can solder in any connector or wire with any orientation you need. We recommend first time Arduino users start with the Uno R3. It's a great board that will get you up and running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
