# Fritzing sketch Bot (saved by Fritzing 0.9.0b)
circuit board: 8.46667cm x 5.64444cm
breadboards: 1

parts:
  Arduino_UNO_R3 = Arduino Uno (Rev3)
  J1 = Basic Servo
  J2 = Basic Servo
  VCC1 = 4 x AAA Battery Mount
  J3 = Infrared Proximity Sensor

nets:
  N1: Arduino_UNO_R3.A0, J3.Vout
  N2: Arduino_UNO_R3.D9_PWM, J1.pulse
  N3: Arduino_UNO_R3.D10_PWM/SS, J2.pulse
  GND: Arduino_UNO_R3.GND, J1.gnd, J2.gnd, VCC1.-, J3.GND
  VCC: Arduino_UNO_R3.5V, J1.vcc, J2.vcc, J3.Vcc
  N4: Arduino_UNO_R3.VIN, VCC1.+
