# Fritzing sketch bot01 (saved by Fritzing 0.9.0b)
breadboards: 1

parts:
  Part1 = Arduino Uno (Rev3)
  J1 = Basic Servo
  J2 = Basic Servo
  VCC1 = 4 x AAA Battery Mount
  J3 = Infrared Proximity Sensor

nets:
  N1: Part1.A0, J3.Vout
  N2: Part1.D9_PWM, J2.pulse
  N3: Part1.D10_PWM/SS, J1.pulse
  VCC: Part1.5V, J1.vcc, J2.vcc, J3.Vcc
  GND: Part1.GND, J1.gnd, J2.gnd, VCC1.-, J3.GND
  N4: Part1.VIN, VCC1.+
