# Fritzing sketch flow2 (saved by Fritzing 0.8.5b)
breadboards: 1

parts:
  Part1 = Arduino Uno (Rev3)
  LED3 = LED - 5mm [color="Green (565nm)" package="5 mm [THT]"]
  R5 = Resistor [tolerance=±5% resistance=220 package=THT]
  S3 = Pushbutton [package="[THT]"]
  R6 = Resistor [tolerance=±5% resistance=10k package=THT]

nets:
  N1: Part1.D8, R5.Pin_1
  N2: Part1.D2, S3.Pin_3, S3.Pin_4, R6.Pin_1
  N3: Part1.GND, LED3.cathode, R6.Pin_0
  N4: LED3.anode, R5.Pin_0
  N5: S3.Pin_1, S3.Pin_2
