# Fritzing sketch flow4 (saved by Fritzing 0.8.5b)
breadboards: 1

parts:
  Part1 = Arduino Uno (Rev3)
  LED1 = LED - 5mm [color="Red (633nm)" package="5 mm [THT]"]
  R1 = Resistor [tolerance=±5% resistance=220 package=THT]
  S1 = Pushbutton [package="[THT]"]
  R2 = Resistor [tolerance=±5% resistance=10k package=THT]
  LED2 = LED - 5mm [color="Yellow (592nm)" package="5 mm [THT]"]
  R3 = Resistor [tolerance=±5% resistance=220 package=THT]
  S2 = Pushbutton [package="[THT]"]
  R4 = Resistor [tolerance=±5% resistance=10k package=THT]
  LED3 = LED - 5mm [color="Green (565nm)" package="5 mm [THT]"]
  R5 = Resistor [tolerance=±5% resistance=220 package=THT]
  S3 = Pushbutton [package="[THT]"]
  R6 = Resistor [tolerance=±5% resistance=10k package=THT]
  J1 = Piezo Speaker
  R7 = Resistor [tolerance=±5% resistance=100 package=THT]

nets:
  N1: Part1.D8, R5.Pin_1
  N2: Part1.D9_PWM, R1.Pin_1
  N3: Part1.D10_PWM/SS, R3.Pin_1
  N4: Part1.D12/MISO, R7.Pin_1
  N5: Part1.D2, S3.Pin_3, S3.Pin_4, R6.Pin_1
  N6: Part1.D3_PWM, S1.Pin_3, S1.Pin_4, R2.Pin_1
  N7: Part1.D4, S2.Pin_3, S2.Pin_4, R4.Pin_1
  N8: Part1.5V, S1.Pin_1, S1.Pin_2, S2.Pin_1, S2.Pin_2
  N9: Part1.GND, LED1.cathode, R2.Pin_0, LED2.cathode, R4.Pin_0, LED3.cathode, R6.Pin_0, J1.pin1
  N10: LED1.anode, R1.Pin_0
  N11: LED2.anode, R3.Pin_0
  N12: LED3.anode, R5.Pin_0
  N13: S3.Pin_1, S3.Pin_2
  N14: J1.pin2, R7.Pin_0
