# Fritzing sketch flow2 (saved by Fritzing 0.8.5b)
breadboards: 1

parts:
  Part1 = Arduino Uno (Rev3)
  S1 = Pushbutton [package="[THT]"]
  LED1 = LED - 5mm [color="Green (560nm)" package="5 mm [THT]"]
  R1 = Resistor [tolerance=±5% resistance=220 package=THT]
  R2 = Resistor [tolerance=±5% resistance=10k package=THT]

nets:
  N1: Part1.D8, R1.Pin_1
  N2: Part1.D2, S1.Pin_1, S1.Pin_2, R2.Pin_0
  N3: Part1.5V, S1.Pin_3, S1.Pin_4
  N4: Part1.GND, LED1.cathode
  N5: LED1.anode, R1.Pin_0
